// Digital circuit MaquinaDeEstados.dig as structural Verilog
module MaquinaDeEstados (
  input  B,
  input  S,
  input  Reset,
  input  Clock,
  output F,
  output A,
  output SF,
  output SA
);

  portao #(.applicationType("GHDL")) u_portao (
    .KEY3(B), .KEY2(S), .KEY1(Reset), .KEY0(Clock), .LEDG7(F), .LEDG6(A), .LEDG1(SF), .LEDG0(SA));

  // Notes on the sheet:
  //   B: KEY(3)
  //   S: KEY(2)
  //   Reset: KEY(1)
  //   Clock: KEY(0)
  //   F: F
  //   A: A
  //   SF: SF
  //   SA: SA
endmodule

/* Code of portao:
LIBRARY ieee;
USE ieee.std_logic_1164.ALL;

ENTITY portao IS PORT (

 
	------ Variáveis ------
	--KEY: in STD_LOGIC_VECTOR(3 downto 0);
	KEY3: in STD_LOGIC;
	KEY2: in STD_LOGIC;
	KEY1: in STD_LOGIC;
	KEY0: in STD_LOGIC;
			-- KEY(3) = B
			-- KEY(2) = S
			-- KEY(1) = Reset
			-- KEY(0) = Clock

	--LEDG: out STD_LOGIC_VECTOR(7 downto 0)
	LEDG7: out STD_LOGIC;
	LEDG6: out STD_LOGIC;
	LEDG1: out STD_LOGIC;
	LEDG0: out STD_LOGIC
			-- LEDG(7) = F
			-- LEDG(6) = A
			-- LEDG(1) = SF
			-- LEDG(0) = SA		
	);
END ENTITY portao;

ARCHITECTURE behave OF portao IS
	--TYPE Tipo_estado IS (A, B, C);
	--SIGNAL nome_estado: Tipo_estado;
	-- Fazer um process (reset, clock) e outro process da lógica da saída (pg 17, 18)
	-- Criar um signal para o F e A 
	--signal SF;-- := LEDG(1);
	--signal SA;--:= LEDG(0);
	--signal F; -- := LEDG(7);
	--signal A; -- := LEDG(6);
	--TYPE tipo_estado IS (Ab,c1,c2,c3,Fc);
	--signal estado := F1;

	TYPE tipo_estado IS (Ab,c1,c2,c3,Fc);
	signal estado : tipo_estado;
	signal A: STD_LOGIC;
	signal F: STD_LOGIC;
	BEGIN
		process(KEY1, KEY0) begin -- Reset e Clock 
			if(KEY1 = '1') then --Reset
				estado <= Fc;
			elsif(KEY0'EVENT AND KEY0 = '0') then
				case estado is
					when Fc =>
						if A = '1' and F = '0' then
							estado <= c1;
						else
							estado <= Fc;
						end if;
					when c1 =>
						if A = '1' and F = '0' then
							estado <= c2;
						elsif F = '1' and A = '0' then
							estado <= Fc;
						else
							estado <= c1;
						end if;
					when c2 =>
						if A = '1' and F = '0' then
							estado <= c3;
						elsif F = '1' and A = '0' then
							estado <= c1;
						else
							estado <= c2;
						end if;
					when c3 =>
						if A = '1' and F = '0' then
							estado <= Ab;
						elsif F = '1' and A = '0' then
							estado <= c2;
						else
							estado <= c3;
						end if;
					when Ab =>
						if F = '1' and A = '0' then
							estado <= c3;
						else
							estado <= Ab;
						end if;
					
				end case;
			end if;	
		end process;
--
--
--
--
		process(estado) begin
			A <= '1';
			LEDG1 <= '1' when estado = Fc else '0';
			LEDG0 <= '1' when estado = Ab else '0';
		end process;


END ARCHITECTURE;
*/
